# Fritzing sketch Protoboard (saved by Fritzing 0.9.3b)
breadboards: 1

parts:
  Componente1 = Arduino Uno (Rev3) - ICSP
  M1 = DC Motor
  Tip122 = npn-Powertransistor [package="TO220 [THT]"]
  U1 = POT [package=pot_alpha_rv16af-20]
  VCC1 = Battery block 9V
  R1 = Resistor [tolerance=±5% resistance=330 package="2010 [SMD]"]
  R2 = Resistor [tolerance=±5% resistance=330 package="0603 [SMD]"]

nets:
  N1: Componente1.A0, U1.S
  N2: Componente1.GND, Tip122.emitter, U1.A, VCC1.-
  N3: Componente1.D3_PWM, R1.Pin_0, R2.Pin_0
  N4: Componente1.5V, U1.E
  N5: M1.pin_1, Tip122.collector
  N6: Tip122.base, R1.Pin_1, R2.Pin_1
